# Fritzing sketch DigiPotLed (saved by Fritzing 0.9.9b)
breadboards: 1

parts:
  Arduino4 = Arduino
  IC3 = IC, DIP package, 8 pins [chip_label=X9C103P spacing=300mil]
  R7 = Resistor [tolerance=±5% resistance=150 power=0.25 package=THT]
  LED1 = Red LED - 5mm [package="5 mm [THT]"]

nets:
  N1: Arduino4.GND, IC3.pin4, IC3.pin6, LED1.cathode
  N2: Arduino4.D4, IC3.pin7
  N3: Arduino4.D3, IC3.pin2
  N4: Arduino4.D2, IC3.pin1
  N5: Arduino4.+5V, IC3.pin3, IC3.pin8
  N6: IC3.pin5, R7.Pin_1
  N7: R7.Pin_0, LED1.anode
